# Fritzing sketch wifiplug (saved by Fritzing 0.9.3b)

parts:
  WeMos_D1_Mini2 = WeMos D1 Mini
  KY-1 = Keyes Relay [package=THT]
  HLK-PM1 = HLK-PM01

nets:
  N1: WeMos_D1_Mini2.5V, KY-1.power, HLK-PM1.+Vo
  N2: WeMos_D1_Mini2.D4, KY-1.signal
  N3: WeMos_D1_Mini2.G, KY-1.ground, HLK-PM1.-Vo

notes:
  AC Wall
  This is the part that goes into the wall.
  AC Plug
  This is where you stick the plug of your appliance into.

custom parts:
  Keyes Relay: The Keyes 5V relay module is suitable for SCM development, home appliance control. It uses a 5V~12V TIL control signal which can control DC / AC signal.
